# Fritzing sketch circuit (saved by Fritzing 0.9.3b)
breadboards: 1

parts:
  U2 = LuaNode32 / ESP32
  부품2 = Soil Moisture Sensor
  DHT1 = DHT11 Humitidy and Temperature Sensor (3 pins)

nets:
  N1: U2.D32, 부품2.SIG
  GND: U2.GND, 부품2.GND, DHT1.Gnd
  3V3: U2.3V3, 부품2.VCC, DHT1.Plus
  N2: U2.D15, DHT1.Signal

custom parts:
  LuaNode32 / ESP32: ESP32 based LuaNode32
  DHT11 Humitidy and Temperature Sensor (3 pins): DHT11 Humidity and Temperature Sensor (3 pins).
